# Fritzing sketch MLX90614 (saved by Fritzing 0.9.2b)
breadboards: 1

parts:
  U1 = MLX90614 [package=to-39]
  C1 = Ceramic Capacitor [capacitance=100nF package="100 mil [THT, multilayer]"]
  Parte1 = Arduino Uno (Rev3) - ICSP
  R1 = Resistor [tolerance=±5% resistance=4.7k package=THT]
  R2 = Resistor [tolerance=±5% resistance=4.7k package=THT]

nets:
  N1: U1.SCL_VZ, C1.0, Parte1.5V, R1.Pin_0, R2.Pin_0
  N2: U1.PWM_SDA, C1.1, Parte1.GND
  N3: U1.VDD, Parte1.A5/SCL, R2.Pin_1
  N4: U1.VSS, Parte1.A4/SDA, R1.Pin_1
